# Fritzing sketch diagram (saved by Fritzing 0.9.3b)
breadboards: 1

parts:
  R1 = Resistor [tolerance=±5% resistance=220 package=THT]
  R2 = Resistor [tolerance=±5% resistance=220 package=THT]
  R3 = Resistor [tolerance=±5% resistance=220 package=THT]
  R4 = Resistor [tolerance=±5% resistance=220 package=THT]
  Part1 = Adafruit T-Cobbler Plus [part_number="Adafruit #1989 and #2028"]
  BUTTON1 = Arcade Button (green)
  BUTTON2 = Arcade Button (red)
  BUTTON3 = Arcade Button (green)
  BUTTON4 = Arcade Button (red)
  R5 = Resistor [tolerance=±5% resistance=220 package=THT]
  R6 = Resistor [tolerance=±5% resistance=220 package=THT]
  R7 = Resistor [tolerance=±5% resistance=220 package=THT]
  R8 = Resistor [tolerance=±5% resistance=220 package=THT]

nets:
  N1: R1.Pin_0, Part1.GPIO20
  N2: R1.Pin_1, BUTTON4.no_name_yet#1, R8.Pin_1
  N3: R2.Pin_0, Part1.GPIO21
  N4: R2.Pin_1, BUTTON1.no_name_yet#1, R7.Pin_1
  N5: R3.Pin_0, Part1.GPIO5
  N6: R3.Pin_1, BUTTON2.no_name_yet#1, R5.Pin_0
  N7: R4.Pin_0, Part1.GPIO6
  N8: R4.Pin_1, BUTTON3.no_name_yet#1, R6.Pin_0
  N9: Part1.+3.3V, BUTTON1.no_name_yet#2, BUTTON2.no_name_yet#2, BUTTON3.no_name_yet#2, BUTTON4.no_name_yet#2
  N10: Part1.GND, R5.Pin_1, R6.Pin_1, R7.Pin_0, R8.Pin_0

custom parts:
  Adafruit T-Cobbler Plus: The Raspberry Pi has landed on the Maker World like a 40-GPIO pinned, quad-USB ported, credit card sized bomb of DIY joy. And while you can use most of our great Model B accessories by hooking up our downgrade cable, its probably a good time to upgrade your set up and accessorize using all of the 40 pins. That's why we now carry the Assembled Adafruit Pi T-Cobbler Plus - Breakout + Cable for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
  Arcade Button (green): Adafruit Arcade Button (green)
  Arcade Button (red): Adafruit Arcade Button (red)
